// Logisim project Guess The Number XTREME.circ as structural Verilog: 11 circuits, main circuit main
module main (
  input  [3:0] in_1,
  input  [3:0] in_2
);

  wire checar_negativo_1_out_3, checar_negativo_2_out_3, Config_2_out, core_1_a_2, core_1_acertou,
       core_1_aganhou, core_1_b_2, core_1_bganhou, core_1_empate, core_1_igual, core_1_maior, core_1_menor,
       core_1_sconfig, core_1_sconfig_2, core_1_sx, core_1_sy, core_1_x, core_1_y, DMA_out, DMB_out,
       \Próximo_out , Reset_out, Start_out, UMA_out, UMB_out;
  wire [3:0] checar_negativo_1_out_2, checar_negativo_2_out_2, core_1_admb, core_1_admb_2, core_1_auma,
       core_1_aumb, core_1_bdma, core_1_bdmb, core_1_buma, core_1_bumb, core_1_placara, core_1_placarb,
       core_1_s_x, core_1_s_y;

  Hex_Digit_Display hex_digit_display_1 (.value(core_1_aumb));  // open: dp
  Hex_Digit_Display hex_digit_display_2 (.value(core_1_auma));  // open: dp
  Hex_Digit_Display hex_digit_display_3 (.value(core_1_admb_2));  // open: dp
  Hex_Digit_Display hex_digit_display_4 (.value(core_1_admb));  // open: dp
  LED Config (.in(core_1_sconfig));
  Hex_Digit_Display hex_digit_display_5 (.value(core_1_placara));  // open: dp
  LED A (.in(core_1_a_2));
  LED SA (.in(checar_negativo_1_out_3));
  Hex_Digit_Display hex_digit_display_6 (.value(checar_negativo_1_out_2));  // open: dp
  Checar_Negativo checar_negativo_1 (.in_1(in_1), .out_2(checar_negativo_1_out_2), .out_3(checar_negativo_1_out_3));
  LED SX (.in(core_1_sx));
  LED X (.in(core_1_x));
  LED A_ganhou (.in(core_1_aganhou));
  Hex_Digit_Display hex_digit_display_7 (.value(core_1_s_x));  // open: dp
  Button Config_2 (.out(Config_2_out));
  Button Reset (.out(Reset_out));
  Button Start (.out(Start_out));
  LED Empate (.in(core_1_empate));
  LED B_ganhou (.in(core_1_bganhou));
  LED SY (.in(core_1_sy));
  Button \Próximo  (.out(\Próximo_out ));
  Button UMB (.out(UMB_out));
  Button UMA (.out(UMA_out));
  Hex_Digit_Display hex_digit_display_8 (.value(core_1_s_y));  // open: dp
  LED Y (.in(core_1_y));
  Button DMA (.out(DMA_out));
  Button DMB (.out(DMB_out));
  LED Maior (.in(core_1_maior));
  LED Igual (.in(core_1_igual));
  LED Menor (.in(core_1_menor));
  LED Acertou (.in(core_1_acertou));
  Core core_1 (
    .PlacarA(core_1_placara), .A(in_1), .B(in_2), .AGanhou(core_1_aganhou), .Empate(core_1_empate),
    .PlacarB(core_1_placarb), .BGanhou(core_1_bganhou), .S_X(core_1_s_x), .S_Y(core_1_s_y),
    .Maior(core_1_maior), .Igual(core_1_igual), .Menor(core_1_menor), .Acertou(core_1_acertou),
    .AUMB(core_1_aumb), .AUMA(core_1_auma), .ADMB(core_1_admb), .ADMB_2(core_1_admb_2), .BUMB(core_1_bumb),
    .BUMA(core_1_buma), .BDMB(core_1_bdmb), .BDMA(core_1_bdma), .A_2(core_1_a_2), .B_2(core_1_b_2),
    .X(core_1_x), .Y(core_1_y), .Reset(Reset_out), .Start(Start_out), .Config(Config_2_out), .UMB(UMB_out),
    .UMA(UMA_out), .DMB(DMB_out), .DMA(DMA_out), .\Próximo (\Próximo_out ), .SConfig(core_1_sconfig),
    .SConfig_2(core_1_sconfig_2), .SX(core_1_sx), .SY(core_1_sy));
  Hex_Digit_Display hex_digit_display_9 (.value(checar_negativo_2_out_2));  // open: dp
  Checar_Negativo checar_negativo_2 (.in_1(in_2), .out_2(checar_negativo_2_out_2), .out_3(checar_negativo_2_out_3));
  Hex_Digit_Display hex_digit_display_10 (.value(core_1_bumb));  // open: dp
  LED Config_3 (.in(core_1_sconfig_2));
  LED B (.in(core_1_b_2));
  LED SB (.in(checar_negativo_2_out_3));
  Hex_Digit_Display hex_digit_display_11 (.value(core_1_placarb));  // open: dp
  Hex_Digit_Display hex_digit_display_12 (.value(core_1_buma));  // open: dp
  Hex_Digit_Display hex_digit_display_13 (.value(core_1_bdmb));  // open: dp
  Hex_Digit_Display hex_digit_display_14 (.value(core_1_bdma));  // open: dp

  // Notes on the sheet:
  //   Placar A
  //   X Chutado
  //   Configurar  Timer
  //   Y Chutado
  //   Placar B
endmodule

module \Cronômetro  (
  input  Config,
  input  UMB,
  input  UMA,
  input  DMB,
  input  DMA,
  input  ENABLE,
  input  RESET,
  input  START,
  output SConfig,
  output D3,
  output A0,
  output B3,
  output D2,
  output C3,
  output A1,
  output B2,
  output D1,
  output C2,
  output A2,
  output B1,
  output D0,
  output C1,
  output A3,
  output B0,
  output C0,
  output DEAD
);

  wire and_1_out, and_2_out, and_3_out, and_4_out, and_5_out, and_6_out, and_8_out, and_9_out, and_10_out,
       and_11_out, and_12_out, and_13_out, and_14_out, checar6_1_s0, checar6_1_s1, checar6_1_s2,
       checar6_2_s0, checar6_2_s1, checar6_2_s2, checar6_2_y, checar10_1_s0, checar10_1_s1, checar10_1_s2,
       checar10_1_s3, checar10_1_y, checar10_2_s0, checar10_2_s1, checar10_2_s2, checar10_2_s3, checar10_2_y,
       clock_1_out, contador5_0_1_s0, contador5_0_1_s1, contador5_0_1_s2, contador5_0_2_s0, contador5_0_2_s1,
       contador5_0_2_s2, contador9_0_1_s0, contador9_0_1_s1, contador9_0_1_s2, contador9_0_1_s3,
       contador9_0_2_s0, contador9_0_2_s1, contador9_0_2_s2, contador9_0_2_s3, d_ff_1_qn, d_ff_2_qn,
       d_ff_3_qn, d_ff_4_qn, d_ff_5_qn, d_ff_6_qn, d_ff_7_qn, d_ff_8_qn, d_ff_9_qn, d_ff_10_qn, d_ff_11_qn,
       d_ff_12_qn, d_ff_13_q, d_ff_14_qn, d_ff_15_qn, not_1_out, not_2_out, not_3_out, not_4_out, not_5_out,
       not_6_out, not_7_out, not_8_out, or_1_out, or_2_out, or_3_out, or_4_out, or_5_out, or_6_out;

  T_Flip_Flop t_ff_1 (.clk(Config), .T(Config), .Q(SConfig), .reset(START));  // open: Qn, preset, en
  not not_1 (not_1_out, SConfig);
  and and_1 (and_1_out, UMB, SConfig);
  or or_1 (or_1_out, and_1_out, and_2_out);
  and and_2 (and_2_out, not_1_out, checar10_1_y, d_ff_13_q, not_2_out);
  not not_2 (not_2_out, and_3_out);
  D_Flip_Flop d_ff_1 (
    .clk(or_1_out), .D(checar6_1_s0), .Q(A2), .Qn(d_ff_1_qn), .en(or_2_out), .reset(RESET));  // open: preset
  or or_2 (or_2_out, SConfig, ENABLE);
  D_Flip_Flop d_ff_2 (
    .clk(or_1_out), .D(checar6_1_s1), .Q(A1), .Qn(d_ff_2_qn), .en(or_2_out), .reset(RESET));  // open: preset
  and and_3 (and_3_out, d_ff_1_qn, d_ff_2_qn, d_ff_3_qn);
  D_Flip_Flop d_ff_3 (
    .clk(or_1_out), .D(checar6_1_s2), .Q(A0), .Qn(d_ff_3_qn), .en(or_2_out), .reset(RESET));  // open: preset
  Contador5_0 contador5_0_1 (
    .A0(A2), .A1(A1), .A2(A0), .S0(contador5_0_1_s0), .S1(contador5_0_1_s1), .S2(contador5_0_1_s2));
  Checar6 checar6_1 (
    .A0(contador5_0_1_s0), .A1(contador5_0_1_s1), .A2(contador5_0_1_s2), .S0(checar6_1_s0),
    .S1(checar6_1_s1), .S2(checar6_1_s2));  // open: Y
  and and_4 (and_4_out, UMA, SConfig);
  or or_3 (or_3_out, and_4_out, and_5_out);
  and and_5 (and_5_out, d_ff_13_q, checar6_2_y, or_4_out, not_3_out);
  not not_3 (not_3_out, SConfig);
  or or_4 (or_4_out, not_4_out, not_5_out);
  not not_4 (not_4_out, and_3_out);
  not not_5 (not_5_out, and_6_out);
  D_Flip_Flop d_ff_4 (
    .clk(or_3_out), .D(checar10_1_s0), .Q(B3), .Qn(d_ff_4_qn), .en(or_2_out), .reset(RESET));  // open: preset
  D_Flip_Flop d_ff_5 (
    .clk(or_3_out), .D(checar10_1_s1), .Q(B2), .Qn(d_ff_5_qn), .en(or_2_out), .reset(RESET));  // open: preset
  and and_6 (and_6_out, d_ff_4_qn, d_ff_5_qn, d_ff_6_qn, d_ff_7_qn);
  D_Flip_Flop d_ff_6 (
    .clk(or_3_out), .D(checar10_1_s2), .Q(B1), .Qn(d_ff_6_qn), .en(or_2_out), .reset(RESET));  // open: preset
  and and_7 (DEAD, and_3_out, and_6_out, and_8_out, and_14_out);
  D_Flip_Flop d_ff_7 (
    .clk(or_3_out), .D(checar10_1_s3), .Q(B0), .Qn(d_ff_7_qn), .en(or_2_out), .reset(RESET));  // open: preset
  and and_8 (and_8_out, d_ff_8_qn, d_ff_9_qn, d_ff_10_qn);
  Contador9_0 contador9_0_1 (
    .A0(B3), .A1(B2), .A2(B1), .A3(B0), .S0(contador9_0_1_s0), .S1(contador9_0_1_s1), .S2(contador9_0_1_s2),
    .S3(contador9_0_1_s3));
  Checar10 checar10_1 (
    .A0(contador9_0_1_s0), .A1(contador9_0_1_s1), .A2(contador9_0_1_s2), .A3(contador9_0_1_s3),
    .S0(checar10_1_s0), .S1(checar10_1_s1), .S2(checar10_1_s2), .S3(checar10_1_s3), .Y(checar10_1_y));
  and and_9 (and_9_out, not_6_out, checar10_2_y, d_ff_13_q);
  not not_6 (not_6_out, SConfig);
  and and_10 (and_10_out, DMB, SConfig);
  or or_5 (or_5_out, and_10_out, and_9_out);
  D_Flip_Flop d_ff_8 (
    .clk(or_5_out), .D(checar6_2_s0), .Q(C2), .Qn(d_ff_8_qn), .en(or_2_out), .reset(RESET));  // open: preset
  D_Flip_Flop d_ff_9 (
    .clk(or_5_out), .D(checar6_2_s1), .Q(C1), .Qn(d_ff_9_qn), .en(or_2_out), .reset(RESET));  // open: preset
  Contador5_0 contador5_0_2 (
    .A0(C2), .A1(C1), .A2(C0), .S0(contador5_0_2_s0), .S1(contador5_0_2_s1), .S2(contador5_0_2_s2));
  D_Flip_Flop d_ff_10 (
    .clk(or_5_out), .D(checar6_2_s2), .Q(C0), .Qn(d_ff_10_qn), .en(or_2_out), .reset(RESET));  // open: preset
  Checar6 checar6_2 (
    .A0(contador5_0_2_s0), .A1(contador5_0_2_s1), .A2(contador5_0_2_s2), .S0(checar6_2_s0),
    .S1(checar6_2_s1), .S2(checar6_2_s2), .Y(checar6_2_y));
  Clock clock_1 (.out(clock_1_out));
  and and_11 (and_11_out, clock_1_out, and_12_out);
  and and_12 (and_12_out, d_ff_13_q, not_8_out, not_7_out);
  not not_7 (not_7_out, DEAD);
  not not_8 (not_8_out, SConfig);
  and and_13 (and_13_out, DMA, SConfig);
  or or_6 (or_6_out, and_13_out, and_11_out);
  D_Flip_Flop d_ff_11 (
    .clk(or_6_out), .D(checar10_2_s0), .Q(D3), .Qn(d_ff_11_qn), .en(or_2_out), .reset(RESET));  // open: preset
  D_Flip_Flop d_ff_12 (
    .clk(or_6_out), .D(checar10_2_s1), .Q(D2), .Qn(d_ff_12_qn), .en(or_2_out), .reset(RESET));  // open: preset
  D_Flip_Flop d_ff_13 (.Q(d_ff_13_q), .preset(START), .reset(SConfig));  // open: clk, D, Qn, en
  D_Flip_Flop d_ff_14 (
    .clk(or_6_out), .D(checar10_2_s2), .Q(D1), .Qn(d_ff_14_qn), .en(or_2_out), .reset(RESET));  // open: preset
  and and_14 (and_14_out, d_ff_11_qn, d_ff_12_qn, d_ff_14_qn, d_ff_15_qn);
  Contador9_0 contador9_0_2 (
    .A0(D3), .A1(D2), .A2(D1), .A3(D0), .S0(contador9_0_2_s0), .S1(contador9_0_2_s1), .S2(contador9_0_2_s2),
    .S3(contador9_0_2_s3));
  D_Flip_Flop d_ff_15 (
    .clk(or_6_out), .D(checar10_2_s3), .Q(D0), .Qn(d_ff_15_qn), .en(or_2_out), .reset(RESET));  // open: preset
  Checar10 checar10_2 (
    .A0(contador9_0_2_s0), .A1(contador9_0_2_s1), .A2(contador9_0_2_s2), .A3(contador9_0_2_s3),
    .S0(checar10_2_s0), .S1(checar10_2_s1), .S2(checar10_2_s2), .S3(checar10_2_s3), .Y(checar10_2_y));

  assign A3 = 1'b0;
  assign C3 = 1'b0;
endmodule

module Contador9_0 (
  input  A0,
  input  A1,
  input  A2,
  input  A3,
  output S0,
  output S1,
  output S2,
  output S3
);

  wire and_1_out, and_2_out, and_3_out, and_4_out, and_5_out, and_6_out, and_7_out, and_8_out, and_9_out,
       and_10_out, and_11_out, and_12_out, not_1_out, not_2_out, not_3_out, not_4_out, not_5_out, not_6_out,
       not_7_out, not_8_out, not_9_out, not_10_out, not_11_out;

  not not_1 (not_1_out, A0);
  not not_2 (not_2_out, A1);
  not not_3 (not_3_out, A2);
  not not_4 (not_4_out, A3);
  and and_1 (and_1_out, A1, A3);
  and and_2 (and_2_out, A1, A2);
  and and_3 (and_3_out, A0, not_5_out);
  not not_5 (not_5_out, A3);
  not not_6 (not_6_out, A2);
  and and_4 (and_4_out, not_6_out, not_7_out);
  not not_7 (not_7_out, A3);
  and and_5 (and_5_out, A2, A3);
  and and_6 (and_6_out, A0, not_8_out);
  not not_8 (not_8_out, A3);
  and and_7 (and_7_out, A2, not_9_out);
  not not_9 (not_9_out, A3);
  and and_8 (and_8_out, A1, not_10_out);
  not not_10 (not_10_out, A3);
  and and_9 (and_9_out, A0, not_11_out);
  not not_11 (not_11_out, A3);
  and and_10 (and_10_out, not_1_out, not_2_out, not_3_out, not_4_out);
  or or_1 (S0, and_10_out, and_11_out, and_12_out);
  and and_11 (and_11_out, A0, A3);
  and and_12 (and_12_out, A0, A2);
  or or_2 (S1, and_1_out, and_2_out, and_3_out);
  or or_3 (S2, and_4_out, and_5_out, and_6_out);
  or or_4 (S3, and_7_out, and_8_out, and_9_out);
endmodule

module Checar6 (
  input  A0,
  input  A1,
  input  A2,
  output S0,
  output S1,
  output S2,
  output Y
);

  wire and_1_out, not_1_out;

  not not_1 (not_1_out, A0);
  and and_1 (and_1_out, A0, A1);
  and and_2 (Y, A0, A2);
  and and_3 (S1, not_1_out, A1);
  or or_1 (S2, A2, and_1_out);

  assign S0 = A0;
endmodule

module Checar10 (
  input  A0,
  input  A1,
  input  A2,
  input  A3,
  output S0,
  output S1,
  output S2,
  output S3,
  output Y
);

  wire and_1_out, and_2_out, and_3_out, and_4_out, and_5_out, not_1_out, not_2_out, not_3_out, not_4_out;

  not not_1 (not_1_out, A0);
  and and_1 (and_1_out, not_1_out, A1);
  and and_2 (and_2_out, A1, not_2_out);
  not not_2 (not_2_out, A3);
  not not_3 (not_3_out, A0);
  and and_3 (and_3_out, not_3_out, A2);
  and and_4 (and_4_out, A0, A1);
  and and_5 (and_5_out, A0, A2);
  not not_4 (not_4_out, A1);
  and and_6 (Y, A0, not_4_out, A3);
  or or_1 (S1, and_1_out, and_2_out);
  or or_2 (S2, and_3_out, and_4_out);
  or or_3 (S3, A3, and_5_out);

  assign S0 = A0;
endmodule

module Contador5_0 (
  input  A0,
  input  A1,
  input  A2,
  output S0,
  output S1,
  output S2
);

  wire and_1_out, and_2_out, and_3_out, and_4_out, and_5_out, and_6_out, not_1_out, not_2_out, not_3_out,
       not_4_out, not_5_out, not_6_out, not_7_out;

  not not_1 (not_1_out, A0);
  not not_2 (not_2_out, A1);
  not not_3 (not_3_out, A2);
  not not_4 (not_4_out, A1);
  not not_5 (not_5_out, A2);
  not not_6 (not_6_out, A2);
  not not_7 (not_7_out, A2);
  and and_1 (and_1_out, not_1_out, not_2_out, not_3_out);
  and and_2 (and_2_out, A0, A2);
  and and_3 (and_3_out, not_4_out, not_5_out);
  and and_4 (and_4_out, A1, A2);
  and and_5 (and_5_out, A1, not_6_out);
  and and_6 (and_6_out, A0, not_7_out);
  or or_1 (S0, and_1_out, and_2_out);
  or or_2 (S1, and_3_out, and_4_out);
  or or_3 (S2, and_5_out, and_6_out);
endmodule

module Game (
  input  \Próximo ,
  input  ADEAD,
  input  BDEAD,
  input  [3:0] A,
  input  Reset,
  input  [3:0] B,
  output Turno,
  output Chutando,
  output [3:0] S_X,
  output [3:0] S_Y,
  output AWin,
  output Maior,
  output Igual,
  output Menor,
  output BWin
);

  wire and_1_out, and_2_out, and_3_out, and_4_out, and_5_out, and_6_out, and_7_out, and_8_out, and_10_out,
       and_11_out, and_12_out, and_13_out, and_14_out, and_15_out, comparator_1_eq, comparator_2_eq,
       comparator_3_eq, comparator_4_eq, comparator_5_eq, comparator_5_gt, comparator_5_lt, comparator_6_eq,
       comparator_6_gt, comparator_6_lt, d_ff_3_q, not_1_out, not_2_out, not_3_out, not_4_out, not_5_out,
       not_6_out, not_7_out, not_8_out, not_9_out, not_10_out, not_11_out, not_12_out, not_13_out,
       not_14_out, not_15_out, or_1_out, or_2_out, or_3_out, or_4_out, or_5_out, or_6_out, proximo_1_s0,
       proximo_1_s1, proximo_1_s2;
  wire [3:0] adder_1_out, adder_2_out, adder_3_out, d_ff_4_q, d_ff_5_q, d_ff_6_q, d_ff_7_q,
       demultiplexer_1_out0, demultiplexer_1_out1, demultiplexer_2_out0, demultiplexer_2_out1,
       multiplexer_1_out, random_1_out, random_2_out;

  not not_1 (not_1_out, d_ff_3_q);
  not not_2 (not_2_out, Chutando);
  not not_3 (not_3_out, d_ff_3_q);
  not not_4 (not_4_out, Chutando);
  D_Flip_Flop d_ff_1 (.clk(\Próximo ), .D(proximo_1_s0), .Q(Turno), .preset(ADEAD), .reset(or_1_out));  // open: Qn, en
  or or_1 (or_1_out, BDEAD, Reset);
  and and_1 (and_1_out, and_7_out, not_1_out, not_2_out, \Próximo );
  or or_2 (or_2_out, and_1_out, and_2_out);
  and and_2 (and_2_out, \Próximo , not_3_out, and_8_out, not_4_out);
  or or_3 (or_3_out, and_1_out, and_2_out);
  D_Flip_Flop d_ff_2 (.clk(\Próximo ), .D(proximo_1_s1), .Q(Chutando), .reset(Reset));  // open: Qn, preset, en
  Multiplexer #(.width(4)) multiplexer_1 (.in0(A), .in1(B), .out(multiplexer_1_out), .sel(Turno));  // open: en
  Random #(.width(4)) random_1 (.clk(or_2_out), .out(random_1_out));  // open: next, clr
  Random #(.width(4), .seed(7)) random_2 (.clk(or_3_out), .out(random_2_out), .clr(or_3_out));  // open: next
  Proximo proximo_1 (.A0(Turno), .A1(Chutando), .A2(d_ff_3_q), .S0(proximo_1_s0), .S1(proximo_1_s1), .S2(proximo_1_s2));
  D_Flip_Flop d_ff_3 (.clk(\Próximo ), .D(proximo_1_s2), .Q(d_ff_3_q), .reset(Reset));  // open: Qn, preset, en
  Demultiplexer #(.width(4)) demultiplexer_1 (
    .out0(demultiplexer_1_out0), .out1(demultiplexer_1_out1), .in(multiplexer_1_out), .sel(Chutando));  // open: en
  not not_5 (not_5_out, Chutando);
  Demultiplexer #(.width(4)) demultiplexer_2 (
    .out0(demultiplexer_2_out0), .out1(demultiplexer_2_out1), .in(multiplexer_1_out), .sel(Chutando));  // open: en
  not not_6 (not_6_out, Turno);
  and and_3 (and_3_out, \Próximo , not_6_out, not_5_out, not_7_out);
  not not_7 (not_7_out, d_ff_3_q);
  not not_8 (not_8_out, Turno);
  and and_4 (and_4_out, \Próximo , not_8_out, Chutando, not_9_out);
  not not_9 (not_9_out, d_ff_3_q);
  and and_5 (and_5_out, \Próximo , Turno, not_10_out, not_11_out);
  not not_10 (not_10_out, Chutando);
  not not_11 (not_11_out, d_ff_3_q);
  and and_6 (and_6_out, \Próximo , Turno, Chutando, not_12_out);
  not not_12 (not_12_out, d_ff_3_q);
  D_Flip_Flop d_ff_4 (
    .clk(and_3_out), .D(demultiplexer_1_out0[0]), .Q(d_ff_4_q[0]), .reset(Reset));  // open: Qn, preset, en
  D_Flip_Flop d_ff_5 (
    .clk(and_4_out), .D(demultiplexer_1_out1[0]), .Q(d_ff_5_q[0]), .reset(Reset));  // open: Qn, preset, en
  D_Flip_Flop d_ff_6 (
    .clk(and_5_out), .D(demultiplexer_2_out0[0]), .Q(d_ff_6_q[0]), .reset(Reset));  // open: Qn, preset, en
  D_Flip_Flop d_ff_7 (
    .clk(and_6_out), .D(demultiplexer_2_out1[0]), .Q(d_ff_7_q[0]), .reset(Reset));  // open: Qn, preset, en
  D_Flip_Flop d_ff_8 (
    .clk(and_3_out), .D(demultiplexer_1_out0[1]), .Q(d_ff_4_q[1]), .reset(Reset));  // open: Qn, preset, en
  D_Flip_Flop d_ff_9 (
    .clk(and_4_out), .D(demultiplexer_1_out1[1]), .Q(d_ff_5_q[1]), .reset(Reset));  // open: Qn, preset, en
  D_Flip_Flop d_ff_10 (
    .clk(and_5_out), .D(demultiplexer_2_out0[1]), .Q(d_ff_6_q[1]), .reset(Reset));  // open: Qn, preset, en
  D_Flip_Flop d_ff_11 (
    .clk(and_6_out), .D(demultiplexer_2_out1[1]), .Q(d_ff_7_q[1]), .reset(Reset));  // open: Qn, preset, en
  D_Flip_Flop d_ff_12 (
    .clk(and_3_out), .D(demultiplexer_1_out0[2]), .Q(d_ff_4_q[2]), .reset(Reset));  // open: Qn, preset, en
  D_Flip_Flop d_ff_13 (
    .clk(and_4_out), .D(demultiplexer_1_out1[2]), .Q(d_ff_5_q[2]), .reset(Reset));  // open: Qn, preset, en
  D_Flip_Flop d_ff_14 (
    .clk(and_5_out), .D(demultiplexer_2_out0[2]), .Q(d_ff_6_q[2]), .reset(Reset));  // open: Qn, preset, en
  D_Flip_Flop d_ff_15 (
    .clk(and_6_out), .D(demultiplexer_2_out1[2]), .Q(d_ff_7_q[2]), .reset(Reset));  // open: Qn, preset, en
  D_Flip_Flop d_ff_16 (
    .clk(and_3_out), .D(demultiplexer_1_out0[3]), .Q(d_ff_4_q[3]), .reset(Reset));  // open: Qn, preset, en
  D_Flip_Flop d_ff_17 (
    .clk(and_4_out), .D(demultiplexer_1_out1[3]), .Q(d_ff_5_q[3]), .reset(Reset));  // open: Qn, preset, en
  D_Flip_Flop d_ff_18 (
    .clk(and_5_out), .D(demultiplexer_2_out0[3]), .Q(d_ff_6_q[3]), .reset(Reset));  // open: Qn, preset, en
  D_Flip_Flop d_ff_19 (
    .clk(and_6_out), .D(demultiplexer_2_out1[3]), .Q(d_ff_7_q[3]), .reset(Reset));  // open: Qn, preset, en
  Comparator #(.width(4), .mode("unsigned")) comparator_1 (
    .a(d_ff_4_q), .b(random_1_out), .eq(comparator_1_eq));  // open: gt, lt
  Comparator #(.width(4), .mode("unsigned")) comparator_2 (
    .a(d_ff_5_q), .b(random_2_out), .eq(comparator_2_eq));  // open: gt, lt
  Comparator #(.width(4), .mode("unsigned")) comparator_3 (
    .a(d_ff_6_q), .b(random_1_out), .eq(comparator_3_eq));  // open: gt, lt
  Comparator #(.width(4), .mode("unsigned")) comparator_4 (
    .a(d_ff_7_q), .b(random_2_out), .eq(comparator_4_eq));  // open: gt, lt
  and and_7 (and_7_out, comparator_1_eq, comparator_2_eq);
  and and_8 (and_8_out, comparator_3_eq, comparator_4_eq);
  and and_9 (BWin, d_ff_3_q, and_8_out);
  Adder #(.width(4)) adder_1 (.a(d_ff_4_q), .b(d_ff_5_q), .out(adder_1_out));  // open: cin, cout
  Adder #(.width(4)) adder_2 (.a(random_1_out), .b(random_2_out), .out(adder_2_out));  // open: cin, cout
  Adder #(.width(4)) adder_3 (.a(d_ff_6_q), .b(d_ff_7_q), .out(adder_3_out));  // open: cin, cout
  not not_13 (not_13_out, Turno);
  Comparator #(.width(4)) comparator_5 (
    .a(adder_1_out), .b(adder_2_out), .gt(comparator_5_gt), .eq(comparator_5_eq), .lt(comparator_5_lt));
  not not_14 (not_14_out, Turno);
  not not_15 (not_15_out, Turno);
  Comparator #(.width(4)) comparator_6 (
    .a(adder_3_out), .b(adder_2_out), .gt(comparator_6_gt), .eq(comparator_6_eq), .lt(comparator_6_lt));
  and and_10 (and_10_out, comparator_5_gt, not_13_out);
  and and_11 (and_11_out, comparator_5_eq, not_14_out);
  or or_4 (or_4_out, and_10_out, and_13_out);
  and and_12 (and_12_out, comparator_5_lt, not_15_out);
  or or_5 (or_5_out, and_11_out, and_14_out);
  and and_13 (and_13_out, comparator_6_gt, Turno);
  or or_6 (or_6_out, and_12_out, and_15_out);
  and and_14 (and_14_out, comparator_6_eq, Turno);
  and and_15 (and_15_out, comparator_6_lt, Turno);
  and and_16 (AWin, d_ff_3_q, and_7_out);
  and and_17 (Maior, or_4_out, d_ff_3_q);
  and and_18 (Igual, or_5_out, d_ff_3_q);
  and and_19 (Menor, or_6_out, d_ff_3_q);
  Multiplexer #(.width(4)) multiplexer_2 (.in0(d_ff_4_q), .in1(d_ff_6_q), .out(S_X), .sel(Turno));  // open: en
  Multiplexer #(.width(4)) multiplexer_3 (.in0(d_ff_5_q), .in1(d_ff_7_q), .out(S_Y), .sel(Turno));  // open: en
endmodule

module Proximo (
  input  A0,
  input  A1,
  input  A2,
  output S0,
  output S1,
  output S2
);

  wire and_1_out, and_2_out, not_1_out, not_2_out, not_4_out;

  not not_1 (not_1_out, A0);
  not not_2 (not_2_out, A2);
  not not_3 (S1, A2);
  not not_4 (not_4_out, A2);
  and and_1 (and_1_out, not_1_out, A2);
  and and_2 (and_2_out, A0, not_2_out);
  and and_3 (S2, A1, not_4_out);
  or or_1 (S0, and_1_out, and_2_out);
endmodule

module Core (
  input  \Próximo ,
  input  [3:0] A,
  input  [3:0] B,
  input  Reset,
  input  Start,
  input  Config,
  input  UMB,
  input  UMA,
  input  DMB,
  input  DMA,
  output AGanhou,
  output Empate,
  output X,
  output Y,
  output [3:0] PlacarA,
  output [3:0] PlacarB,
  output A_2,
  output B_2,
  output [3:0] S_X,
  output BGanhou,
  output SX,
  output [3:0] S_Y,
  output SY,
  output Maior,
  output Igual,
  output Menor,
  output [3:0] AUMB,
  output [3:0] AUMA,
  output [3:0] ADMB,
  output [3:0] ADMB_2,
  output [3:0] BUMB,
  output [3:0] BUMA,
  output [3:0] BDMB,
  output [3:0] BDMA,
  output Acertou,
  output SConfig,
  output SConfig_2
);

  wire and_1_out, and_2_out, and_3_out, and_4_out, comparator_1_eq, comparator_1_gt, comparator_1_lt,
       \cronômetro_1_dead , \cronômetro_2_dead , game_1_awin, game_1_bwin, not_1_out, not_2_out, not_4_out,
       not_6_out, not_7_out, not_8_out, or_1_out, or_2_out, or_4_out, or_5_out, placar_1_out_4,
       placar_2_out_4;
  wire [3:0] game_1_s_x, game_1_s_y;

  \Cronômetro  \cronômetro_1  (
    .A0(AUMB[0]), .D3(ADMB_2[3]), .C2(ADMB[2]), .A1(AUMB[1]), .D2(ADMB_2[2]), .C1(ADMB[1]), .A2(AUMB[2]),
    .D1(ADMB_2[1]), .C0(ADMB[0]), .D0(ADMB_2[0]), .DMA(DMA), .DMB(DMB), .UMA(UMA), .UMB(UMB),
    .ENABLE(and_1_out), .DEAD(\cronômetro_1_dead ), .RESET(Reset), .B3(AUMA[3]), .B2(AUMA[2]), .B1(AUMA[1]),
    .B0(AUMA[0]), .START(Start), .A3(AUMB[3]), .C3(ADMB[3]), .SConfig(SConfig), .Config(Config));
  and and_1 (and_1_out, not_1_out, or_1_out);
  not not_1 (not_1_out, or_4_out);
  or or_1 (or_1_out, not_2_out, Config);
  not not_2 (not_2_out, B_2);
  \Cronômetro  \cronômetro_2  (
    .A0(BUMB[0]), .D3(BDMA[3]), .C2(BDMB[2]), .A1(BUMB[1]), .D2(BDMA[2]), .C1(BDMB[1]), .A2(BUMB[2]),
    .D1(BDMA[1]), .C0(BDMB[0]), .D0(BDMA[0]), .DMA(DMA), .DMB(DMB), .UMA(UMA), .UMB(UMB), .ENABLE(and_2_out),
    .DEAD(\cronômetro_2_dead ), .RESET(Reset), .B3(BUMA[3]), .B2(BUMA[2]), .B1(BUMA[1]), .B0(BUMA[0]),
    .START(Start), .A3(BUMB[3]), .C3(BDMB[3]), .SConfig(SConfig_2), .Config(Config));
  not not_3 (A_2, B_2);
  not not_4 (not_4_out, or_4_out);
  and and_2 (and_2_out, not_4_out, or_2_out);
  or or_2 (or_2_out, B_2, Config);
  not not_5 (X, Y);
  Game game_1 (
    .\Próximo (and_3_out), .ADEAD(\cronômetro_1_dead ), .BDEAD(\cronômetro_2_dead ), .A(A), .B(B),
    .Turno(B_2), .Chutando(Y), .S_X(game_1_s_x), .S_Y(game_1_s_y), .AWin(game_1_awin), .Maior(Maior),
    .Igual(Igual), .Menor(Menor), .BWin(game_1_bwin), .Reset(Reset));
  and and_3 (and_3_out, not_6_out, not_7_out, \Próximo , not_8_out);
  not not_6 (not_6_out, or_4_out);
  not not_7 (not_7_out, or_5_out);
  Checar_Negativo checar_negativo_1 (.in_1(game_1_s_x), .out_2(S_X), .out_3(SX));
  Checar_Negativo checar_negativo_2 (.in_1(game_1_s_y), .out_2(S_Y), .out_3(SY));
  not not_8 (not_8_out, SConfig_2);
  Placar placar_1 (.in_1(game_1_awin), .in_2(Reset), .out_3(PlacarA), .out_4(placar_1_out_4));
  Placar placar_2 (.in_1(game_1_bwin), .in_2(Reset), .out_3(PlacarB), .out_4(placar_2_out_4));
  or or_3 (Acertou, game_1_awin, game_1_bwin);
  or or_4 (or_4_out, placar_2_out_4, placar_1_out_4);
  Comparator #(.width(4), .mode("unsigned")) comparator_1 (
    .a(PlacarA), .b(PlacarB), .gt(comparator_1_gt), .eq(comparator_1_eq), .lt(comparator_1_lt));
  and and_4 (and_4_out, \cronômetro_1_dead , \cronômetro_2_dead );
  or or_5 (or_5_out, or_4_out, and_4_out);
  and and_5 (AGanhou, comparator_1_gt, or_5_out);
  and and_6 (Empate, comparator_1_eq, or_5_out);
  and and_7 (BGanhou, comparator_1_lt, or_5_out);
endmodule

module Placar (
  input  in_1,
  input  in_2,
  output [3:0] out_3,
  output out_4
);

  wire [3:0] adder_1_out;

  D_Flip_Flop d_ff_1 (.clk(in_1), .D(adder_1_out[0]), .Q(out_3[0]), .reset(in_2));  // open: Qn, preset, en
  D_Flip_Flop d_ff_2 (.clk(in_1), .D(adder_1_out[1]), .Q(out_3[1]), .reset(in_2));  // open: Qn, preset, en
  D_Flip_Flop d_ff_3 (.clk(in_1), .D(adder_1_out[2]), .Q(out_3[2]), .reset(in_2));  // open: Qn, preset, en
  D_Flip_Flop d_ff_4 (.clk(in_1), .D(adder_1_out[3]), .Q(out_3[3]), .reset(in_2));  // open: Qn, preset, en
  Comparator #(.width(4)) comparator_1 (.a(out_3), .b(4'b1111), .eq(out_4));  // open: gt, lt
  Adder #(.width(4)) adder_1 (.a(out_3), .b(4'b0001), .out(adder_1_out));  // open: cin, cout
endmodule

module Checar_Negativo (
  input  [3:0] in_1,
  output [3:0] out_2,
  output out_3
);

  wire [3:0] adder_1_out, demultiplexer_1_out0, demultiplexer_1_out1, not_1_out;

  Demultiplexer #(.width(4)) demultiplexer_1 (
    .out0(demultiplexer_1_out0), .out1(demultiplexer_1_out1), .in(in_1), .sel(in_1[3]));  // open: en
  assign not_1_out = ~demultiplexer_1_out1;  // NOT_Gate not_1, 4 bits wide
  Adder #(.width(4)) adder_1 (.a(not_1_out), .b(4'b0001), .out(adder_1_out));  // open: cin, cout
  assign out_2 = demultiplexer_1_out0 | adder_1_out;  // OR_Gate or_1, 4 bits wide

  assign out_3 = in_1[3];
endmodule
